// Digital circuit 1bit_register.dig as structural Verilog
module _1bit_register (
  input  Din,
  input  Sel,
  input  Clock,
  output Dout
);

  wire multiplexer_1_out;

  Multiplexer multiplexer_1 (.sel(Sel), .in_0(Dout), .in_1(Din), .out(multiplexer_1_out));
  D_FF d_ff_1 (.D(multiplexer_1_out), .C(Clock), .Q(Dout));  // open: nQ
endmodule
