// Digital circuit 1x15-SRAM.dig as structural Verilog
module _1x15_SRAM (
  input  RS1,
  input  RS2,
  input  WS,
  input  [14:0] WD_14_0,
  input  CLK,
  output [14:0] RD1_14_0,
  output [14:0] RD2_14_0
);

  wire RD1_1;

  // _1x1_RAM _1x1_ram_1: pin names not known; wires that end beside it: WD_14_0[0], WS, RS1, RS2, CLK, RD1_14_0[0], RD2_14_0[0]
  // _1x1_RAM _1x1_ram_2: pin names not known; wires that end beside it: WD_14_0[5], WS, RS1, RS2, CLK, RD1_14_0[5], RD2_14_0[5]
  // _1x1_RAM _1x1_ram_3: pin names not known; wires that end beside it: WD_14_0[10], WS, RS1, RS2, CLK, RD1_14_0[10], RD2_14_0[10]
  // _1x1_RAM _1x1_ram_4: pin names not known; wires that end beside it: WD_14_0[1], WS, RS1, RS2, CLK, RD1_1, RD1_14_0[1]
  // _1x1_RAM _1x1_ram_5: pin names not known; wires that end beside it: WD_14_0[11], WS, RS1, RS2, CLK, RD1_14_0[11], RD2_14_0[11]
  // _1x1_RAM _1x1_ram_6: pin names not known; wires that end beside it: WD_14_0[6], WS, RS1, RS2, CLK, RD1_14_0[6], RD2_14_0[6]
  // _1x1_RAM _1x1_ram_7: pin names not known; wires that end beside it: WD_14_0[2], WS, RS1, RS2, CLK, RD1_14_0[2], RD2_14_0[2]
  // _1x1_RAM _1x1_ram_8: pin names not known; wires that end beside it: WD_14_0[7], WS, RS1, RS2, CLK, RD1_14_0[7], RD2_14_0[7]
  // _1x1_RAM _1x1_ram_9: pin names not known; wires that end beside it: WD_14_0[12], WS, RS1, RS2, CLK, RD1_14_0[12], RD2_14_0[12]
  // _1x1_RAM _1x1_ram_10: pin names not known; wires that end beside it: WD_14_0[3], WS, RS1, RS2, CLK, RD1_14_0[3], RD2_14_0[3]
  // _1x1_RAM _1x1_ram_11: pin names not known; wires that end beside it: WD_14_0[8], WS, RS1, RS2, CLK, RD1_14_0[8], RD2_14_0[8]
  // _1x1_RAM _1x1_ram_12: pin names not known; wires that end beside it: WD_14_0[13], WS, RS1, RS2, CLK, RD1_14_0[13], RD2_14_0[13]
  // _1x1_RAM _1x1_ram_13: pin names not known; wires that end beside it: WD_14_0[4], WS, RS1, RS2, CLK, RD1_14_0[4], RD2_14_0[4]
  // _1x1_RAM _1x1_ram_14: pin names not known; wires that end beside it: WD_14_0[9], WS, RS1, RS2, CLK, RD1_14_0[9], RD2_14_0[9]
  // _1x1_RAM _1x1_ram_15: pin names not known; wires that end beside it: WD_14_0[14], WS, RS1, RS2, CLK, RD1_14_0[14], RD2_14_0[14]

  assign RD2_14_0[1] = RD1_14_0[1];

  // Other names for the same wires on the sheet: RD1_0 = RD1_14_0[0]; RD1_2 = RD1_14_0[2]; RD1_3 = RD1_14_0[3];
  //   RD1_4 = RD1_14_0[4]; RD1_5 = RD1_14_0[5]; RD1_6 = RD1_14_0[6]; RD1_7 = RD1_14_0[7]; RD1_8 = RD1_14_0[8];
  //   RD1_9 = RD1_14_0[9]; RD1_10 = RD1_14_0[10]; RD1_11 = RD1_14_0[11]; RD1_12 = RD1_14_0[12]; RD1_13 = RD1_14_0[13];
  //   RD1_14 = RD1_14_0[14]; RD2_0 = RD2_14_0[0]; RD2_1 = RD1_14_0[1]; RD2_2 = RD2_14_0[2]; RD2_3 = RD2_14_0[3];
  //   RD2_4 = RD2_14_0[4]; RD2_5 = RD2_14_0[5]; RD2_6 = RD2_14_0[6]; RD2_7 = RD2_14_0[7]; RD2_8 = RD2_14_0[8];
  //   RD2_9 = RD2_14_0[9]; RD2_10 = RD2_14_0[10]; RD2_11 = RD2_14_0[11]; RD2_12 = RD2_14_0[12]; RD2_13 = RD2_14_0[13];
  //   RD2_14 = RD2_14_0[14]; WD0 = WD_14_0[0]; WD1 = WD_14_0[1]; WD2 = WD_14_0[2]; WD3 = WD_14_0[3]; WD4 = WD_14_0[4];
  //   WD5 = WD_14_0[5]; WD6 = WD_14_0[6]; WD7 = WD_14_0[7]; WD8 = WD_14_0[8]; WD9 = WD_14_0[9]; WD10 = WD_14_0[10];
  //   WD11 = WD_14_0[11]; WD12 = WD_14_0[12]; WD13 = WD_14_0[13]; WD14 = WD_14_0[14]
endmodule
