// Digital circuit 5-bit-Registet-Set.dig as structural Verilog
module _5_bit_Registet_Set (
  input  [1:0] RA_1_0,
  input  [1:0] RB_1_0,
  input  [1:0] WR_1_0,
  input  WE,
  input  [4:0] WRD_4_0,
  input  Clock,
  output [4:0] A_4_0,
  output [4:0] B_4_0
);

  wire A0, A1, A2, D0, D1, D2, decoder_1_out_3;
  wire [4:0] R0, R1, R2;

  and and_1 (D0, WE, A0);
  and and_2 (D1, WE, A1);
  and and_3 (D2, WE, A2);
  Decoder #(.Selector_Bits(2)) decoder_1 (.sel(WR_1_0), .out_0(A0), .out_1(A1), .out_2(A2), .out_3(decoder_1_out_3));
  _5bit_register__1 _5bit_register__1_1 (.Din_4_0(WRD_4_0), .Sel(D0), .Clock(Clock), .Dout_4_0(R0));
  _5bit_register__1 _5bit_register__1_2 (.Din_4_0(WRD_4_0), .Sel(D1), .Clock(Clock), .Dout_4_0(R1));
  _5bit_register__1 _5bit_register__1_3 (.Din_4_0(WRD_4_0), .Sel(D2), .Clock(Clock), .Dout_4_0(R2));
  Multiplexer #(.Selector_Bits(2), .Bits(5)) multiplexer_1 (
    .sel(RA_1_0), .in_0(R0), .in_1(R1), .in_2(R2), .in_3({5{1'b0}}), .out(A_4_0));
  Multiplexer #(.Selector_Bits(2), .Bits(5)) multiplexer_2 (
    .sel(RB_1_0), .in_0(R0), .in_1(R1), .in_2(R2), .in_3({5{1'b0}}), .out(B_4_0));
  // also tied to GND on the sheet: decoder_1_out_3
endmodule
