// Digital circuit 5bit_register (1).dig as structural Verilog
module _5bit_register__1 (
  input  [4:0] Din_4_0,
  input  Sel,
  input  Clock,
  output [4:0] Dout_4_0
);

  _1bit_register _1bit_register_1 (.Din(Din_4_0[0]), .Sel(Sel), .Clock(Clock), .Dout(Dout_4_0[0]));
  _1bit_register _1bit_register_2 (.Din(Din_4_0[1]), .Sel(Sel), .Clock(Clock), .Dout(Dout_4_0[1]));
  _1bit_register _1bit_register_3 (.Din(Din_4_0[2]), .Sel(Sel), .Clock(Clock), .Dout(Dout_4_0[2]));
  _1bit_register _1bit_register_4 (.Din(Din_4_0[3]), .Sel(Sel), .Clock(Clock), .Dout(Dout_4_0[3]));
  _1bit_register _1bit_register_5 (.Din(Din_4_0[4]), .Sel(Sel), .Clock(Clock), .Dout(Dout_4_0[4]));
endmodule
