// Digital circuit ALU-Circuit.dig as structural Verilog
module ALU_Circuit (
  input  [4:0] A_4_0,
  input  [4:0] B_4_0,
  input  [1:0] op_1_0,
  output [4:0] R_4_0
);

  wire [4:0] _5Bit_AND_r_4_0, _5Bit_Left_Rotator_o_4_0, _5bitadder_1_s_4_0;

  _5BitAdder _5bitadder_1 (.A_4_0(A_4_0), .B_4_0(B_4_0), .S_4_0(_5bitadder_1_s_4_0));  // open: Cout
  _5BitROL _5Bit_Left_Rotator (.A_4_0(A_4_0), .B_2_0(B_4_0[2:0]), .O_4_0(_5Bit_Left_Rotator_o_4_0));
  AND _5Bit_AND (.A_4_0(A_4_0), .B_4_0(B_4_0), .R_4_0(_5Bit_AND_r_4_0));
  Multiplexer #(.Selector_Bits(2), .Bits(5)) multiplexer_1 (
    .sel(op_1_0), .in_0(_5bitadder_1_s_4_0), .in_1(_5Bit_Left_Rotator_o_4_0), .in_2(_5Bit_AND_r_4_0),
    .in_3({5{1'b0}}), .out(R_4_0));

  // Other names for the same wires on the sheet: A[4:0] = A_4_0; B[4:0] = B_4_0
endmodule
