// Digital circuit CPU.dig as structural Verilog
module CPU (
  input  [3:0] WA_3_0,
  input  WS,
  input  [14:0] WD_14_0,
  input  CLK,
  input  PC_EN,
  input  [3:0] RA2_3_0,
  input  SF,
  input  ZF,
  output [14:0] RD2,
  output [4:0] RES,
  output [3:0] Label,
  output [4:0] A,
  output [4:0] B
);

  wire CPU_CLK, Imm_sel, Jmp_sel, REG_en;
  wire [1:0] op;
  wire [3:0] _4bit_pc_adder_1_o_3_0, multiplexer_1_out, opcode;
  wire [3:2] Jmp_addr;
  wire [4:0] _5_bit_registet_set_1_b_4_0;
  wire [4:3] Imm_val;
  wire [6:0] Don_t_care;

  Multiplexer #(.Bits(4)) multiplexer_1 (
    .sel(Jmp_sel), .in_0(_4bit_pc_adder_1_o_3_0), .in_1({Jmp_addr, Imm_val}), .out(multiplexer_1_out));
  // _4bit_program_counter _4bit_program_counter_1: pin names not known; wires that end beside it: multiplexer_1_out, CPU_CLK, Label
  and and_1 (CPU_CLK, CLK, PC_EN);
  _4bit_PC_Adder _4bit_pc_adder_1 (.I_3_0(Label), .O_3_0(_4bit_pc_adder_1_o_3_0));
  _9x15_SRAM _9x15_sram_1 (
    .RA1_3_0(Label), .RA2_3_0(RA2_3_0), .WA_3_0(WA_3_0), .WS(WS), .WD_14_0(WD_14_0), .CLK(CLK),
    .RD1_14_0({opcode, Jmp_addr, Imm_val, Don_t_care}), .RD2_14_0(RD2));
  _5_bit_Registet_Set _5_bit_registet_set_1 (
    .RA_1_0(Jmp_addr), .RB_1_0(Imm_val), .WR_1_0(Jmp_addr), .WE(REG_en), .WRD_4_0(RES), .Clock(CPU_CLK),
    .A_4_0(A), .B_4_0(_5_bit_registet_set_1_b_4_0));
  Multiplexer #(.Bits(5)) multiplexer_2 (
    .sel(Imm_sel), .in_0(_5_bit_registet_set_1_b_4_0), .in_1({Imm_val, Don_t_care[6:4]}), .out(B));
  CU cu_1 (.Opcode_3_0(opcode), .SF(SF), .ZF(ZF), .Op_1_0(op), .REG_EN(REG_en), .Imm_Sel(Imm_sel), .Jmp_Sel(Jmp_sel));
  ALU_Circuit alu_circuit_1 (.A_4_0(A), .B_4_0(B), .op_1_0(op), .R_4_0(RES));

  // Other names for the same wires on the sheet: Imm_val[2:0] = Don_t_care[6:4]; Jmp_addr[1:0] = Imm_val;
  //   R2[1:0] = Imm_val; R1[1:0] = Jmp_addr; RA2[3:0] = RA2_3_0; Result[4:0] = RES; WA[3:0] = WA_3_0;
  //   WD[14:0] = WD_14_0

  // Notes on the sheet:
  //   Register Mode(Type of operation[00]) = 2bit(Type of Operation)+2bit(ALU operation)+2bit(Register1)+2bit(Regsiter2)+7bit(Dont care)
  //   Immediate mode(Type of operation[01]) = 2bit(Type of Operation)+2bit(ALU operation)+2bit(Register1)+5bit(Imm value)+4bit(Dont care)
  //   Jump mode(Type of operation[10]) = 2bit(Type of Operation)+2bit(ALU operation)+4bit(jmp value)+7bit(Dont care)
  //   Add(Op=00),ROL(01),AND(OP=10)
  //   Label-----operation(Assembly code)  -----	 Machine code
  //   0000  -----	ADD R0,5	---->	010000001010000
  //   0001  -----	ADD R1,4	---->	010001001000000
  //   0010  -----	ADD R0,R1	---->	000000010000000
  //   0011  -----	JLE 0010	---->	100100100000000
  //   0100  -----	ROL R0,2	---->	010101000100000
  //   0101  -----	AND R0.R1	---->	001000010000000
  //   0110  -----	JMP 0100	---->	100001000000000
endmodule
