// Digital circuit CU_.dig as structural Verilog
module CU (
  input  [3:0] Opcode_3_0,
  input  SF,
  input  ZF,
  output [1:0] Op_1_0,
  output REG_EN,
  output Imm_Sel,
  output Jmp_Sel
);

  wire and_1_out, and_3_out, and_4_out, and_5_out, or_1_out, or_2_out;

  or or_1 (or_1_out, SF, ZF);
  and and_1 (and_1_out, ~Opcode_3_0[2], ~Opcode_3_0[3]);  // And
  and and_2 (Imm_Sel, Opcode_3_0[2], ~Opcode_3_0[3]);  // And
  and and_3 (and_3_out, ~Opcode_3_0[2], Opcode_3_0[3]);  // And
  and and_4 (and_4_out, ~Opcode_3_0[0], ~Opcode_3_0[1]);  // And
  and and_5 (and_5_out, Opcode_3_0[0], ~Opcode_3_0[1], or_1_out);  // And
  or or_2 (or_2_out, and_4_out, and_5_out);
  or or_3 (REG_EN, and_1_out, Imm_Sel);
  and and_6 (Jmp_Sel, and_3_out, or_2_out);

  assign Op_1_0 = Opcode_3_0[1:0];
endmodule
